# Fritzing sketch sonde (saved by Fritzing 0.9.3b)
circuit board: 7.00001cm x 7.00001cm

parts:
  470 = Resistor [tolerance=±5% resistance=470 package=THT]
  D2/SDA = male pin header, 2 pins [form="♂ (male)"]
  3_3v = male pin header, 1 pin [form="♂ (male)"]
  Mux_4051 = 74HC4051 [package="DIP (Dual Inline) [THT]"]
  SR501 = male pin header, 3 pins [form="♂ (male)"]
  LX1972 = male pin header, 3 pins [form="♂ (male)"]
  5v = male pin header, 4 pins [form="♂ (male)"]
  Gnd = male pin header, 4 pins [form="♂ (male)"]
  RX/TX = male pin header, 2 pins [form="♂ (male)"]
  WeMos_D1_Mini = WeMos D1 Mini
  A5 = male pin header, 5 pins [form="♂ (male)"]
  D4 = male pin header, 1 pin [form="♂ (male)"]
  ws2812b = screw terminal, 3 pins
  MQ-135 = male pin header, 4 pins [form="♂ (male)"]
  MQ-7 = male pin header, 4 pins [form="♂ (male)"]
  BME_280 = male pin header, 4 pins [form="♂ (male)"]
  D0 = male pin header, 1 pin [form="♂ (male)"]
  Supply = screw terminal, 3 pins
  1000uf = Capacitor Polarized [package=cpol-radial-1000uf-25v]

nets:
  N1: 470.Pin_0, ws2812b.pin3
  N2: 470.Pin_1, WeMos_D1_Mini.D3
  N3: D2/SDA.pin1, WeMos_D1_Mini.D1, BME_280.pin2
  N4: D2/SDA.pin2, WeMos_D1_Mini.D2, BME_280.pin1
  N5: 3_3v.pin1, WeMos_D1_Mini.3V3
  N6: Mux_4051.IO4, A5.pin2
  N7: Mux_4051.IO6, A5.pin3
  N8: Mux_4051.IO, WeMos_D1_Mini.A0
  N9: Mux_4051.IO7, A5.pin4
  N10: Mux_4051.IO5, A5.pin5
  N11: Mux_4051.INH, Mux_4051.VEE, Mux_4051.VSS, SR501.pin3, LX1972.pin3, Gnd.pin1, Gnd.pin2, Gnd.pin3, Gnd.pin4, WeMos_D1_Mini.G, ws2812b.pin2, MQ-135.pin3, MQ-7.pin3, BME_280.pin3, Supply.pin2, 1000uf.-
  N12: Mux_4051.C, WeMos_D1_Mini.D7
  N13: Mux_4051.B, WeMos_D1_Mini.D6
  N14: Mux_4051.A, WeMos_D1_Mini.D5
  N15: Mux_4051.IO3, LX1972.pin2
  N16: Mux_4051.IO0, A5.pin1
  N17: Mux_4051.IO1, MQ-7.pin1
  N18: Mux_4051.IO2, MQ-135.pin1
  VDD: Mux_4051.VDD, SR501.pin1, LX1972.pin1, 5v.pin1, 5v.pin2, 5v.pin3, 5v.pin4, WeMos_D1_Mini.5V, ws2812b.pin1, MQ-135.pin4, MQ-7.pin4, BME_280.pin4, Supply.pin1, 1000uf.+
  N19: SR501.pin2, WeMos_D1_Mini.D8
  N20: RX/TX.pin1, WeMos_D1_Mini.TX
  N21: RX/TX.pin2, WeMos_D1_Mini.RX
  N22: WeMos_D1_Mini.D0, D0.pin1
  N23: WeMos_D1_Mini.D4, D4.pin1
  N24: WeMos_D1_Mini.RST, Supply.pin3

notes:
  D1/SCL
  A7
  A6
  A4
  A1
  A2
  A3
  5v
  Gnd
  Rst
  D3
  D8
  D5
  D6
  D7
  A0
  Home Sensor
  Gazz

custom parts:
  74HC4051: 8 channel analog multiplexer/demultiplexer
